# Fritzing sketch 7segmentos (saved by Fritzing 0.9.3b)

parts:
  Componente1 = Arduino Mega 2560 (Rev3)
  8x8_LED_Modul_mit_MAX1 = 8x8 LED Modul mit MAX7219 [package=THT]

nets:
  N1: Componente1.5V, 8x8_LED_Modul_mit_MAX1.VCC_Eingang
  N2: Componente1.GND, 8x8_LED_Modul_mit_MAX1.GND_Eingang
  N3: Componente1.D27, 8x8_LED_Modul_mit_MAX1.CS_Eingang
  N4: Componente1.D28, 8x8_LED_Modul_mit_MAX1.DIN_Eingang
  N5: Componente1.D32, 8x8_LED_Modul_mit_MAX1.CLK_Eingang
