# Fritzing sketch bus (saved by Fritzing 0.9.3b)
breadboards: 1

parts:
  Componente1 = Analog Digital MUX Breakout
  Componente2 = Arduino Mega 2560 (Rev3)
  LCD1 = LCD screen  # not connected
  J1 = female pin header, 3 pins [form="♀ (female)"]

nets:
  N1: Componente1.GND, J1.pin2
  VCC: Componente1.VCC, Componente2.5V
  N2: Componente1.EN, J1.pin3
  N3: Componente1.S0, Componente2.D22
  N4: Componente1.S1, Componente2.D23
  N5: Componente1.S2, Componente2.D24
  N6: Componente1.S3, Componente2.D25
  N7: Componente1.SIG, Componente2.D7_PWM
  N8: Componente2.GND, J1.pin1

notes:
  BUS
