# Fritzing sketch button (saved by Fritzing 0.9.3b)
breadboards: 1

parts:
  Componente1 = Arduino Mega 2560 (Rev3)
  S1 = Pushbutton [package="[SMD]"]
  S2 = Pushbutton [package="[SMD]"]

nets:
  N1: Componente1.GND, S1.Pin_3, S1.Pin_4, S2.Pin_3, S2.Pin_4
  N2: Componente1.D38, S1.Pin_1, S1.Pin_2
  N3: Componente1.D39, S2.Pin_1, S2.Pin_2
