# Fritzing sketch encoder_pulsador (saved by Fritzing 0.9.3b)

parts:
  Componente1 = Arduino Mega 2560 (Rev3)
  SW1 = ENCODER_RGB_CA [package=encoder_led_3]

nets:
  N1: Componente1.GND, SW1.-G, SW1.A
  N2: Componente1.D3_PWM, SW1.+
  N3: Componente1.D6_PWM, SW1.SW
  N4: Componente1.D7_PWM, SW1.-R
