# Fritzing sketch encoder_simple (saved by Fritzing 0.9.3b)

parts:
  Componente1 = Arduino Mega 2560 (Rev3)
  RE1 = Rotary Encoder [package=THT]

nets:
  N1: Componente1.GND, RE1.EncoderPinC
  N2: Componente1.D6_PWM, RE1.EncoderPinB
  N3: Componente1.D7_PWM, RE1.EncoderPinA
