# Fritzing sketch lcd (saved by Fritzing 0.9.3b)

parts:
  Componente2 = Arduino Mega 2560 (Rev3)
  LCD1 = LCD screen
  J1 = female alternating pin header, 3 pins [form="♀ (female)"]

nets:
  5V: Componente2.5V, LCD1.VDD
  N1: Componente2.GND, J1.pin1
  N2: Componente2.D22, LCD1.DB4
  N3: Componente2.D23, LCD1.DB5
  N4: Componente2.D24, LCD1.DB6
  N5: Componente2.D25, LCD1.DB7
  N6: Componente2.D28, LCD1.RS
  N7: Componente2.D32, LCD1.E
  N8: LCD1.VSS, J1.pin3
  N9: LCD1.R/W, J1.pin2

notes:
  BUS
