# Fritzing sketch mux (saved by Fritzing 0.9.3b)
breadboards: 1

parts:
  Componente1 = Analog Digital MUX Breakout
  Componente2 = Arduino Mega 2560 (Rev3)
  S1 = Pushbutton [package="[THT]"]
  S2 = Pushbutton [package="[THT]"]
  S3 = Pushbutton [package="[THT]"]
  S4 = Pushbutton [package="[THT]"]

nets:
  N1: Componente1.C0, S1.Pin_1, S1.Pin_2
  N2: Componente1.C1, S2.Pin_1, S2.Pin_2
  N3: Componente1.C2, S3.Pin_1, S3.Pin_2
  N4: Componente1.C3, S4.Pin_1, S4.Pin_2
  GND: Componente1.GND, Componente2.GND, S1.Pin_3, S1.Pin_4, S2.Pin_3, S2.Pin_4, S3.Pin_3, S3.Pin_4, S4.Pin_3, S4.Pin_4
  VCC: Componente1.VCC, Componente2.5V
  N5: Componente1.S0, Componente2.D22
  N6: Componente1.S1, Componente2.D23
  N7: Componente1.S2, Componente2.D24
  N8: Componente1.S3, Componente2.D25
  N9: Componente1.SIG, Componente2.D7_PWM

notes:
  BUS
