# Fritzing sketch switch (saved by Fritzing 0.9.3b)

parts:
  Componente1 = Arduino Uno (Rev3)
  S1 = SWITCH-MOMENTARY-2 [package=tactile-switch-1101ne]

nets:
  N1: Componente1.D13/SCK, S1.2
  N2: Componente1.GND, S1.1
