# Fritzing sketch switch_multiple (saved by Fritzing 0.9.3b)

parts:
  Componente1 = Analog Digital MUX Breakout
  Componente2 = Arduino Mega 2560 (Rev3)
  S2 = SPST Switch [package=ayz0202]

nets:
  N1: Componente1.C0, S2.P
  N2: Componente1.C1, S2.S
  GND: Componente1.GND, Componente2.GND, S2.O
  VCC: Componente1.VCC, Componente2.5V
  N3: Componente1.S0, Componente2.D22
  N4: Componente1.S1, Componente2.D23
  N5: Componente1.S2, Componente2.D24
  N6: Componente1.S3, Componente2.D25
  N7: Componente1.SIG, Componente2.D7_PWM

notes:
  BUS
